// Logisim project Logisim.circ as structural Verilog: 16 circuits, main circuit MAIN CIRCUIT
module MAIN_CIRCUIT (
);

  wire _1_out, _2_out, _3_out, _4_out, _5_out, _6_out, _7_out, _8_out, _9_out, and_1_out, and_2_out,
       button_1_out, button_2_out, button_3_out, button_4_out, counter_1_a0, counter_1_a1, counter_1_a2,
       counter_1_a3, initial_state_generator_1__1, initial_state_generator_1__2,
       initial_state_generator_1__3, initial_state_generator_1__4, initial_state_generator_1__5,
       initial_state_generator_1__6, initial_state_generator_1__7, initial_state_generator_1__8,
       initial_state_generator_1__9, input_controller_1__1o, input_controller_1__2o, input_controller_1__3o,
       input_controller_1__4o, input_controller_1__5o, input_controller_1__6o, input_controller_1__7o,
       input_controller_1__8o, input_controller_1__9o, input_generator_to_different_ffs_1_f1,
       input_generator_to_different_ffs_1_f2, input_generator_to_different_ffs_1_f3,
       input_generator_to_different_ffs_1_f4, input_generator_to_different_ffs_1_f5,
       input_generator_to_different_ffs_1_f6, input_generator_to_different_ffs_1_f7,
       input_generator_to_different_ffs_1_f8, input_generator_to_different_ffs_1_f9,
       input_supplier_to_ff_1__1o, input_supplier_to_ff_1__2o, input_supplier_to_ff_1__3o,
       input_supplier_to_ff_1__4o, input_supplier_to_ff_1__5o, input_supplier_to_ff_1__6o,
       input_supplier_to_ff_1__7o, input_supplier_to_ff_1__8o, input_supplier_to_ff_1__9o, lcd_decoder_1_a,
       lcd_decoder_1_b, lcd_decoder_1_c, lcd_decoder_1_d, lcd_decoder_1_e, lcd_decoder_1_f, lcd_decoder_1_g,
       lcd_decoder_2_a, lcd_decoder_2_b, lcd_decoder_2_c, lcd_decoder_2_d, lcd_decoder_2_e, lcd_decoder_2_f,
       lcd_decoder_2_g, moves_calucalator_1_a0, moves_calucalator_1_a1, moves_calucalator_1_a2,
       moves_calucalator_1_a3, nor_1_out, not_1_out, not_2_out, not_3_out, not_4_out, not_5_out, or_1_out,
       or_2_out, shift_register_1_output, solution_generator_1__1fd, solution_generator_1__2_2,
       solution_generator_1__3_2, solution_generator_1__4_2, solution_generator_1__5_2,
       solution_generator_1__6_2, solution_generator_1__7_2, solution_generator_1__8_2,
       solution_generator_1__9_2, t_ff_1_q, t_ffs_1_q1, t_ffs_1_q2, t_ffs_1_q3, t_ffs_1_q4, t_ffs_1_q5,
       t_ffs_1_q6, t_ffs_1_q7, t_ffs_1_q8, t_ffs_1_q9, total_moves_counter_1_a1, total_moves_counter_1_a2,
       total_moves_counter_1_b1, total_moves_counter_1_b2, total_moves_counter_1_c1,
       total_moves_counter_1_c2, total_moves_counter_1_d1, total_moves_counter_1_d2, total_moves_counter_1_e,
       total_moves_counter_1_e2, total_moves_counter_1_f1, total_moves_counter_1_f2,
       total_moves_counter_1_g2, total_moves_counter_1_gg1, total_moves_counter_1_max, xnor_1_out;

  Initial_State_Generator initial_state_generator_1 (
    .reset(button_2_out), .high(not_1_out), ._1(initial_state_generator_1__1),
    ._2(initial_state_generator_1__2), ._3(initial_state_generator_1__3), ._4(initial_state_generator_1__4),
    ._5(initial_state_generator_1__5), ._6(initial_state_generator_1__6), ._7(initial_state_generator_1__7),
    ._8(initial_state_generator_1__8), ._9(initial_state_generator_1__9));
  Input_Controller input_controller_1 (
    ._1(_1_out), ._2(_2_out), ._3(_3_out), ._4(_4_out), ._5(_5_out), ._6(_6_out), ._7(_7_out), ._8(_8_out),
    ._9(_9_out), .result(not_5_out), ._1o(input_controller_1__1o), ._2o(input_controller_1__2o),
    ._3o(input_controller_1__3o), ._4o(input_controller_1__4o), ._5o(input_controller_1__5o),
    ._6o(input_controller_1__6o), ._7o(input_controller_1__7o), ._8o(input_controller_1__8o),
    ._9o(input_controller_1__9o));
  Input__Supplier_To_Flip_Flop input_supplier_to_ff_1 (
    ._1(initial_state_generator_1__1), ._2(initial_state_generator_1__2), ._3(initial_state_generator_1__3),
    ._4(initial_state_generator_1__4), ._5(initial_state_generator_1__5), ._6(initial_state_generator_1__6),
    ._7(initial_state_generator_1__7), ._8(initial_state_generator_1__8), ._9(initial_state_generator_1__9),
    ._1a(input_generator_to_different_ffs_1_f1), ._2a(input_generator_to_different_ffs_1_f2),
    ._3a(input_generator_to_different_ffs_1_f3), ._4a(input_generator_to_different_ffs_1_f4),
    ._5a(input_generator_to_different_ffs_1_f5), ._6a(input_generator_to_different_ffs_1_f6),
    ._7a(input_generator_to_different_ffs_1_f7), ._8a(input_generator_to_different_ffs_1_f8),
    ._9a(input_generator_to_different_ffs_1_f9), ._1o(input_supplier_to_ff_1__1o),
    ._2o(input_supplier_to_ff_1__2o), ._3o(input_supplier_to_ff_1__3o), ._4o(input_supplier_to_ff_1__4o),
    ._5o(input_supplier_to_ff_1__5o), ._6o(input_supplier_to_ff_1__6o), ._7o(input_supplier_to_ff_1__7o),
    ._8o(input_supplier_to_ff_1__8o), ._9o(input_supplier_to_ff_1__9o));
  Button button_1 (.out(button_1_out));
  not not_1 (not_1_out, button_1_out);
  Input_Generator_to_Different_Flip_Flops input_generator_to_different_ffs_1 (
    ._1(input_controller_1__1o), ._2(input_controller_1__2o), ._3(input_controller_1__3o),
    ._4(input_controller_1__4o), ._5(input_controller_1__5o), ._6(input_controller_1__6o),
    ._7(input_controller_1__7o), ._8(input_controller_1__8o), ._9(input_controller_1__9o),
    .F1(input_generator_to_different_ffs_1_f1), .F2(input_generator_to_different_ffs_1_f2),
    .F3(input_generator_to_different_ffs_1_f3), .F4(input_generator_to_different_ffs_1_f4),
    .F5(input_generator_to_different_ffs_1_f5), .F6(input_generator_to_different_ffs_1_f6),
    .F7(input_generator_to_different_ffs_1_f7), .F8(input_generator_to_different_ffs_1_f8),
    .F9(input_generator_to_different_ffs_1_f9));
  or or_1 (or_1_out, input_controller_1__9o, input_controller_1__8o, input_controller_1__7o, input_controller_1__6o, input_controller_1__5o, input_controller_1__4o, input_controller_1__3o, input_controller_1__2o, input_controller_1__1o);
  and and_1 (and_1_out, or_1_out, ~total_moves_counter_1_max);  // AND_Gate
  Button _1 (.out(_1_out));
  Button _4 (.out(_4_out));
  Button _7 (.out(_7_out));
  not not_2 (not_2_out, not_1_out);
  T_Flip_Flops t_ffs_1 (
    ._1(input_supplier_to_ff_1__1o), ._2(input_supplier_to_ff_1__2o), ._3(input_supplier_to_ff_1__3o),
    ._4(input_supplier_to_ff_1__4o), ._5(input_supplier_to_ff_1__5o), ._6(input_supplier_to_ff_1__6o),
    ._7(input_supplier_to_ff_1__7o), ._8(input_supplier_to_ff_1__8o), ._9(input_supplier_to_ff_1__9o),
    .q1(t_ffs_1_q1), .q2(t_ffs_1_q2), .q3(t_ffs_1_q3), .q4(t_ffs_1_q4), .q5(t_ffs_1_q5), .q6(t_ffs_1_q6),
    .q7(t_ffs_1_q7), .q8(t_ffs_1_q8), .q9(t_ffs_1_q9), .high(not_1_out));
  Button _2 (.out(_2_out));
  Button _5 (.out(_5_out));
  Button _8 (.out(_8_out));
  Button _3 (.out(_3_out));
  Button _6 (.out(_6_out));
  Button _9 (.out(_9_out));
  Total_Moves_counter total_moves_counter_1 (
    .high(not_1_out), .clk(and_1_out), .reset(button_2_out), .a2(total_moves_counter_1_a2),
    .b2(total_moves_counter_1_b2), .c2(total_moves_counter_1_c2), .d2(total_moves_counter_1_d2),
    .e2(total_moves_counter_1_e2), .f2(total_moves_counter_1_f2), .g2(total_moves_counter_1_g2),
    .a1(total_moves_counter_1_a1), .b1(total_moves_counter_1_b1), .c1(total_moves_counter_1_c1),
    .d1(total_moves_counter_1_d1), .e(total_moves_counter_1_e), .f1(total_moves_counter_1_f1),
    .gg1(total_moves_counter_1_gg1), .max(total_moves_counter_1_max));
  Button button_2 (.out(button_2_out));
  _7_Segment_Display u_7_segment_display_1 (
    .g(total_moves_counter_1_g2), .f(total_moves_counter_1_f2), .a(total_moves_counter_1_a2),
    .b(total_moves_counter_1_b2), .e(total_moves_counter_1_e2), .d(total_moves_counter_1_d2),
    .c(total_moves_counter_1_c2));  // open: dp
  Button button_3 (.out(button_3_out));
  or or_2 (or_2_out, button_3_out, button_4_out);
  Counter counter_1 (
    .clk(or_2_out), .high(not_1_out), .reset(button_2_out), .a0(counter_1_a0), .a1(counter_1_a1),
    .a2(counter_1_a2), .a3(counter_1_a3));
  _7_Segment_Display u_7_segment_display_2 (
    .g(total_moves_counter_1_gg1), .f(total_moves_counter_1_f1), .a(total_moves_counter_1_a1),
    .b(total_moves_counter_1_b1), .e(total_moves_counter_1_e), .d(total_moves_counter_1_d1),
    .c(total_moves_counter_1_c1));  // open: dp
  Button button_4 (.out(button_4_out));
  LED led_1 (.in(shift_register_1_output));
  _7_Segment_Display u_7_segment_display_3 (
    .g(lcd_decoder_1_g), .f(lcd_decoder_1_f), .a(lcd_decoder_1_a), .b(lcd_decoder_1_b), .e(lcd_decoder_1_e),
    .d(lcd_decoder_1_d), .c(lcd_decoder_1_c));  // open: dp
  LCD_Decoder lcd_decoder_1 (
    ._3(counter_1_a3), ._2(counter_1_a2), ._1(counter_1_a1), ._0(counter_1_a0), .a(lcd_decoder_1_a),
    .b(lcd_decoder_1_b), .c(lcd_decoder_1_c), .d(lcd_decoder_1_d), .e(lcd_decoder_1_e), .f(lcd_decoder_1_f),
    .g(lcd_decoder_1_g));
  and and_2 (and_2_out, ~total_moves_counter_1_max, nor_1_out);  // AND_Gate
  LED YOU_WON (.in(and_2_out));
  LED led_2 (.in(t_ffs_1_q1));
  LED led_3 (.in(t_ffs_1_q4));
  LED led_4 (.in(t_ffs_1_q7));
  LED led_5 (.in(t_ffs_1_q2));
  LED led_6 (.in(t_ffs_1_q5));
  LED led_7 (.in(t_ffs_1_q8));
  LED led_8 (.in(t_ffs_1_q3));
  LED led_9 (.in(t_ffs_1_q6));
  LED led_10 (.in(t_ffs_1_q9));
  not not_3 (not_3_out, button_3_out);
  not not_4 (not_4_out, button_4_out);
  xnor xnor_1 (xnor_1_out, not_4_out, not_3_out);
  _7_Segment_Display u_7_segment_display_4 (
    .g(lcd_decoder_2_g), .f(lcd_decoder_2_f), .a(lcd_decoder_2_a), .b(lcd_decoder_2_b), .e(lcd_decoder_2_e),
    .d(lcd_decoder_2_d), .c(lcd_decoder_2_c));  // open: dp
  Solution_Generator solution_generator_1 (
    ._1(t_ffs_1_q1), ._2(t_ffs_1_q2), ._3(t_ffs_1_q3), ._4(t_ffs_1_q4), .in_5(not_2_out), ._5(t_ffs_1_q5),
    ._6(t_ffs_1_q6), ._7(t_ffs_1_q7), ._8(t_ffs_1_q8), ._9(t_ffs_1_q9), ._1fd(solution_generator_1__1fd),
    ._2_2(solution_generator_1__2_2), ._3_2(solution_generator_1__3_2), ._4_2(solution_generator_1__4_2),
    ._5_2(solution_generator_1__5_2), ._6_2(solution_generator_1__6_2), ._7_2(solution_generator_1__7_2),
    ._8_2(solution_generator_1__8_2), ._9_2(solution_generator_1__9_2));
  Shift_Register shift_register_1 (
    .load_1__shift_0(button_3_out), .en(not_1_out), .clk_falling_edge(xnor_1_out), .reset(button_2_out),
    ._9(solution_generator_1__9_2), ._8(solution_generator_1__8_2), ._7(solution_generator_1__7_2),
    ._6(solution_generator_1__6_2), ._5(solution_generator_1__5_2), ._4(solution_generator_1__4_2),
    ._3(solution_generator_1__3_2), ._2(solution_generator_1__2_2), ._1(solution_generator_1__1fd),
    .\output (shift_register_1_output));
  T_Flip_Flop t_ff_1 (.clk(button_3_out), .T(not_1_out), .Q(t_ff_1_q), .reset(button_2_out));  // open: Qn, preset, en
  LCD_Decoder lcd_decoder_2 (
    ._3(moves_calucalator_1_a3), ._2(moves_calucalator_1_a2), ._1(moves_calucalator_1_a1),
    ._0(moves_calucalator_1_a0), .a(lcd_decoder_2_a), .b(lcd_decoder_2_b), .c(lcd_decoder_2_c),
    .d(lcd_decoder_2_d), .e(lcd_decoder_2_e), .f(lcd_decoder_2_f), .g(lcd_decoder_2_g));
  nor nor_1 (nor_1_out, t_ffs_1_q1, t_ffs_1_q2, t_ffs_1_q3, t_ffs_1_q4, t_ffs_1_q5, t_ffs_1_q6, t_ffs_1_q7, t_ffs_1_q8, t_ffs_1_q9);
  Moves_Calucalator moves_calucalator_1 (
    .i(solution_generator_1__1fd), .i_2(solution_generator_1__2_2), .i_3(solution_generator_1__3_2),
    .i_4(solution_generator_1__4_2), .i_5(solution_generator_1__5_2), .i_6(solution_generator_1__6_2),
    .i_7(solution_generator_1__7_2), .i_8(solution_generator_1__8_2), .i_9(solution_generator_1__9_2),
    .hint(t_ff_1_q), .a0(moves_calucalator_1_a0), .a1(moves_calucalator_1_a1), .a2(moves_calucalator_1_a2),
    .a3(moves_calucalator_1_a3));
  not not_5 (not_5_out, nor_1_out);

  // Notes on the sheet:
  //   NOTE:
  //   *
  //    then press GREEN button to get next move(hint)
  //   INPUT PAD
  //   INPUTS TO THE GAME
  //       RESET game
  //   ^
  //   press this once to go 
  //    automatic mode 
  //   ^
  //   next hint
  //   Toatal No of 
  //   MOVES
  //   used
  //   Maximum Moves
  //   Alowed 39
  //   HINT
  //   LED
  //   ^
  //   press this to get
  //    press RESET button to start the game  .  To go to automatic mode press the white button first once. Then if hint led is on then press the coressponding button in input pad 
  //   see the INSTRUCTION MODULE to know the GamePlay
  //   if LED is HIGH press the corresponding button 
  //    shown in LCD to finish the game in automatic mode
  //   OUTPUT display
  //   ^
  //   STAGE
  //      works only when automatic mode is on
  //   Minimum No of 
  //   MOVES required
  //   to WIN from
  //   CURRENT 
endmodule

// Input Generator
module Input_Generator_to_Different_Flip_Flops (
  input  _1,
  input  _2,
  input  _3,
  input  _4,
  input  _5,
  input  _6,
  input  _7,
  input  _8,
  input  _9,
  output F1,
  output F2,
  output F3,
  output F4,
  output F5,
  output F6,
  output F7,
  output F8,
  output F9
);

  or or_1 (F1, _4, _2, _1);
  or or_2 (F2, _5, _3, _2, _1);
  or or_3 (F3, _6, _3, _2);
  or or_4 (F4, _7, _5, _4, _1);
  or or_5 (F5, _8, _6, _5, _4, _2);
  or or_6 (F6, _9, _6, _5, _3);
  or or_7 (F7, _8, _7, _4);
  or or_8 (F8, _9, _8, _7, _5);
  or or_9 (F9, _9, _8, _6);

  // Notes on the sheet:
  //   By:
  //   16CO142
  //   16CO144
endmodule

module Solution_Generator (
  input  _1,
  input  _2,
  input  _3,
  input  _4,
  input  in_5,
  input  _5,
  input  _6,
  input  _7,
  input  _8,
  input  _9,
  output _1fd,
  output _2_2,
  output _3_2,
  output _4_2,
  output _5_2,
  output _6_2,
  output _7_2,
  output _8_2,
  output _9_2
);

  Odd_No_of_1_s_Checker odd_no_of_1_s_checker_1 (.in_1(_1), .in_2(_3), .in_3(_6), .in_4(_7), .in_5(_8), .out_6(_1fd));
  Odd_No_of_1_s_Checker odd_no_of_1_s_checker_2 (.in_1(_5), .in_2(_7), .in_3(in_5), .in_4(_8), .in_5(_9), .out_6(_2_2));
  Odd_No_of_1_s_Checker odd_no_of_1_s_checker_3 (.in_1(_1), .in_2(_4), .in_3(_3), .in_4(_8), .in_5(_9), .out_6(_3_2));
  Odd_No_of_1_s_Checker odd_no_of_1_s_checker_4 (.in_1(_6), .in_2(_3), .in_3(in_5), .in_4(_5), .in_5(_9), .out_6(_4_2));
  Odd_No_of_1_s_Checker odd_no_of_1_s_checker_5 (.in_1(_2), .in_2(_4), .in_3(_5), .in_4(_6), .in_5(_8), .out_6(_5_2));
  Odd_No_of_1_s_Checker odd_no_of_1_s_checker_6 (.in_1(_1), .in_2(_4), .in_3(in_5), .in_4(_7), .in_5(_5), .out_6(_6_2));
  Odd_No_of_1_s_Checker odd_no_of_1_s_checker_7 (.in_1(_1), .in_2(_2), .in_3(_6), .in_4(_7), .in_5(_9), .out_6(_7_2));
  Odd_No_of_1_s_Checker odd_no_of_1_s_checker_8 (.in_1(_2), .in_2(_1), .in_3(in_5), .in_4(_3), .in_5(_5), .out_6(_8_2));
  Odd_No_of_1_s_Checker odd_no_of_1_s_checker_9 (.in_1(_2), .in_2(_3), .in_3(_4), .in_4(_7), .in_5(_9), .out_6(_9_2));

  // Notes on the sheet:
  //   By:
  //   16CO142
  //   16CO144
endmodule

module Odd_No_of_1_s_Checker (
  input  in_1,
  input  in_2,
  input  in_3,
  input  in_4,
  input  in_5,
  output out_6
);

  wire xor_1_out, xor_2_out, xor_3_out;

  xor xor_1 (xor_1_out, in_1, in_2);
  xor xor_2 (xor_2_out, xor_1_out, in_3);
  xor xor_3 (xor_3_out, xor_2_out, in_4);
  xor xor_4 (out_6, xor_3_out, in_5);

  // Notes on the sheet:
  //   By:
  //   16CO142
  //   16CO144
endmodule

// Solution Storer
module Shift_Register (
  input  _9,
  input  _8,
  input  _7,
  input  _6,
  input  _5,
  input  _1,
  input  _4,
  input  _3,
  input  _2,
  input  load_1__shift_0,
  input  en,
  input  clk_falling_edge,
  input  reset,
  output \output 
);

  wire and_1_out, and_2_out, and_3_out, and_4_out, and_5_out, and_6_out, and_7_out, and_8_out, and_9_out,
       and_10_out, and_11_out, and_12_out, and_13_out, and_14_out, and_15_out, and_16_out, d_ff_1_q,
       d_ff_2_q, d_ff_3_q, d_ff_4_q, d_ff_5_q, d_ff_6_q, d_ff_7_q, d_ff_8_q, not_1_out, or_1_out, or_2_out,
       or_3_out, or_4_out, or_5_out, or_6_out, or_7_out, or_8_out;

  not not_1 (not_1_out, load_1__shift_0);
  and and_1 (and_1_out, d_ff_1_q, not_1_out);
  or or_1 (or_1_out, and_1_out, and_2_out);
  D_Flip_Flop #(.trigger("falling")) d_ff_1 (
    .clk(clk_falling_edge), .D(_9), .Q(d_ff_1_q), .en(en), .reset(reset));  // open: Qn, preset
  and and_2 (and_2_out, load_1__shift_0, _8);
  and and_3 (and_3_out, d_ff_2_q, not_1_out);
  D_Flip_Flop #(.trigger("falling")) d_ff_2 (
    .clk(clk_falling_edge), .D(or_1_out), .Q(d_ff_2_q), .en(en), .reset(reset));  // open: Qn, preset
  and and_4 (and_4_out, load_1__shift_0, _7);
  or or_2 (or_2_out, and_3_out, and_4_out);
  D_Flip_Flop #(.trigger("falling")) d_ff_3 (
    .clk(clk_falling_edge), .D(or_2_out), .Q(d_ff_3_q), .en(en), .reset(reset));  // open: Qn, preset
  and and_5 (and_5_out, load_1__shift_0, _6);
  and and_6 (and_6_out, d_ff_3_q, not_1_out);
  or or_3 (or_3_out, and_6_out, and_5_out);
  and and_7 (and_7_out, d_ff_4_q, not_1_out);
  D_Flip_Flop #(.trigger("falling")) d_ff_4 (
    .clk(clk_falling_edge), .D(or_3_out), .Q(d_ff_4_q), .en(en), .reset(reset));  // open: Qn, preset
  and and_8 (and_8_out, load_1__shift_0, _5);
  or or_4 (or_4_out, and_7_out, and_8_out);
  and and_9 (and_9_out, d_ff_5_q, not_1_out);
  and and_10 (and_10_out, load_1__shift_0, _4);
  or or_5 (or_5_out, and_9_out, and_10_out);
  D_Flip_Flop #(.trigger("falling")) d_ff_5 (
    .clk(clk_falling_edge), .D(or_4_out), .Q(d_ff_5_q), .en(en), .reset(reset));  // open: Qn, preset
  and and_11 (and_11_out, d_ff_6_q, not_1_out);
  or or_6 (or_6_out, and_11_out, and_13_out);
  D_Flip_Flop #(.trigger("falling")) d_ff_6 (
    .clk(clk_falling_edge), .D(or_5_out), .Q(d_ff_6_q), .en(en), .reset(reset));  // open: Qn, preset
  and and_12 (and_12_out, d_ff_7_q, not_1_out);
  and and_13 (and_13_out, load_1__shift_0, _3);
  D_Flip_Flop #(.trigger("falling")) d_ff_7 (
    .clk(clk_falling_edge), .D(or_6_out), .Q(d_ff_7_q), .en(en), .reset(reset));  // open: Qn, preset
  and and_14 (and_14_out, load_1__shift_0, _2);
  or or_7 (or_7_out, and_12_out, and_14_out);
  and and_15 (and_15_out, d_ff_8_q, not_1_out);
  and and_16 (and_16_out, load_1__shift_0, _1);
  or or_8 (or_8_out, and_15_out, and_16_out);
  D_Flip_Flop #(.trigger("falling")) d_ff_8 (
    .clk(clk_falling_edge), .D(or_7_out), .Q(d_ff_8_q), .en(en), .reset(reset));  // open: Qn, preset
  D_Flip_Flop #(.trigger("falling")) d_ff_9 (
    .clk(clk_falling_edge), .D(or_8_out), .Q(\output ), .en(en), .reset(reset));  // open: Qn, preset

  // Notes on the sheet:
  //   By:
  //   16CO142
  //   16CO144
endmodule

module LCD_Decoder (
  input  _3,
  input  _2,
  input  _1,
  input  _0,
  output a,
  output b,
  output c,
  output d,
  output e,
  output f,
  output g
);

  wire and_1_out, and_2_out, and_3_out, and_4_out, and_5_out, and_6_out, and_7_out, and_8_out, and_9_out,
       and_10_out, and_11_out, and_12_out, and_13_out, and_14_out, not_1_out, not_2_out, not_3_out,
       xnor_1_out;

  not not_1 (not_1_out, _2);
  not not_2 (not_2_out, _1);
  not not_3 (not_3_out, _0);
  or or_1 (c, _3, _2, not_2_out, _0);
  and and_1 (and_1_out, _1, not_3_out);
  and and_2 (and_2_out, not_1_out, not_3_out);
  and and_3 (and_3_out, not_1_out, _1);
  and and_4 (and_4_out, _2, not_2_out, _0);
  and and_5 (and_5_out, _1, not_3_out);
  and and_6 (and_6_out, not_1_out, not_3_out);
  and and_7 (and_7_out, _2, not_2_out);
  and and_8 (and_8_out, _2, not_3_out);
  and and_9 (and_9_out, not_2_out, not_3_out);
  and and_10 (and_10_out, _1, not_1_out);
  and and_11 (and_11_out, _1, not_3_out);
  and and_12 (and_12_out, _2, not_2_out);
  xnor xnor_1 (xnor_1_out, _0, _2);
  and and_13 (and_13_out, not_2_out, not_3_out);
  and and_14 (and_14_out, _0, _1);
  or or_2 (e, and_5_out, and_6_out);
  or or_3 (f, and_7_out, and_8_out, and_9_out, _3);
  or or_4 (g, and_10_out, and_11_out, and_12_out, _3);
  or or_5 (a, xnor_1_out, _3, _1);
  or or_6 (b, and_13_out, and_14_out, _3, not_1_out);
  or or_7 (d, and_1_out, and_2_out, and_3_out, and_4_out, _3);

  // Notes on the sheet:
  //   By:
  //   16CO142
  //   16CO144
endmodule

module Counter (
  input  clk,
  input  high,
  input  reset,
  output a0,
  output a1,
  output a2,
  output a3
);

  wire and_1_out, or_1_out, t_ff_1_qn, t_ff_2_qn, t_ff_3_qn;

  T_Flip_Flop t_ff_1 (.clk(clk), .T(high), .Q(a0), .Qn(t_ff_1_qn), .reset(or_1_out));  // open: preset, en
  or or_1 (or_1_out, reset, and_1_out);
  T_Flip_Flop t_ff_2 (.clk(t_ff_1_qn), .T(high), .Q(a1), .Qn(t_ff_2_qn), .reset(or_1_out));  // open: preset, en
  T_Flip_Flop t_ff_3 (.clk(t_ff_2_qn), .T(high), .Q(a2), .Qn(t_ff_3_qn), .reset(or_1_out));  // open: preset, en
  T_Flip_Flop t_ff_4 (.clk(t_ff_3_qn), .T(high), .Q(a3), .reset(or_1_out));  // open: Qn, preset, en
  and and_1 (and_1_out, a1, a3);

  // Notes on the sheet:
  //   By:
  //   16CO142
  //   16CO144
endmodule

// Initial state Generator
module Initial_State_Generator (
  input  reset,
  input  high,
  output _9,
  output _8,
  output _1,
  output _5,
  output _7,
  output _2,
  output _3,
  output _4,
  output _6
);

  wire d_ff_1_q, d_ff_2_q, d_ff_3_q, d_ff_4_q, d_ff_5_q, d_ff_6_q, d_ff_7_q, d_ff_8_q, d_ff_9_q, d_ff_9_qn,
       xor_1_out;

  ExactlyOne xor_1 (.out(xor_1_out), .in0(d_ff_9_qn), .in1(d_ff_6_q), .in2(d_ff_4_q), .in3(d_ff_1_q));
  D_Flip_Flop d_ff_1 (.clk(reset), .D(xor_1_out), .Q(d_ff_1_q), .en(high));  // open: Qn, preset, reset
  and and_1 (_1, d_ff_1_q, reset);
  D_Flip_Flop d_ff_2 (.clk(reset), .D(d_ff_1_q), .Q(d_ff_2_q), .en(high));  // open: Qn, preset, reset
  and and_2 (_2, d_ff_2_q, reset);
  D_Flip_Flop d_ff_3 (.clk(reset), .D(d_ff_2_q), .Q(d_ff_3_q), .en(high));  // open: Qn, preset, reset
  and and_3 (_3, d_ff_3_q, reset);
  D_Flip_Flop d_ff_4 (.clk(reset), .D(d_ff_3_q), .Q(d_ff_4_q), .en(high));  // open: Qn, preset, reset
  and and_4 (_4, d_ff_4_q, reset);
  D_Flip_Flop d_ff_5 (.clk(reset), .D(d_ff_4_q), .Q(d_ff_5_q), .en(high));  // open: Qn, preset, reset
  and and_5 (_5, d_ff_5_q, reset);
  D_Flip_Flop d_ff_6 (.clk(reset), .D(d_ff_5_q), .Q(d_ff_6_q), .en(high));  // open: Qn, preset, reset
  and and_6 (_6, d_ff_6_q, reset);
  D_Flip_Flop d_ff_7 (.clk(reset), .D(d_ff_6_q), .Q(d_ff_7_q), .en(high));  // open: Qn, preset, reset
  and and_7 (_7, d_ff_7_q, reset);
  D_Flip_Flop d_ff_8 (.clk(reset), .D(d_ff_7_q), .Q(d_ff_8_q), .en(high));  // open: Qn, preset, reset
  and and_8 (_8, reset, d_ff_8_q);
  and and_9 (_9, reset, d_ff_9_q);
  D_Flip_Flop d_ff_9 (.clk(reset), .D(d_ff_8_q), .Q(d_ff_9_q), .Qn(d_ff_9_qn), .en(high));  // open: preset, reset
endmodule

// Input Selector
module Input__Supplier_To_Flip_Flop (
  input  _1,
  input  _2,
  input  _3,
  input  _4,
  input  _5,
  input  _6,
  input  _7,
  input  _8,
  input  _9,
  input  _1a,
  input  _2a,
  input  _3a,
  input  _4a,
  input  _5a,
  input  _6a,
  input  _7a,
  input  _8a,
  input  _9a,
  output _1o,
  output _2o,
  output _3o,
  output _4o,
  output _5o,
  output _6o,
  output _7o,
  output _8o,
  output _9o
);

  or or_1 (_1o, _1, _1a);
  or or_2 (_2o, _2, _2a);
  or or_3 (_3o, _3, _3a);
  or or_4 (_4o, _4, _4a);
  or or_5 (_5o, _5, _5a);
  or or_6 (_6o, _6, _6a);
  or or_7 (_7o, _7, _7a);
  or or_8 (_8o, _8, _8a);
  or or_9 (_9o, _9, _9a);

  // Notes on the sheet:
  //   By:
  //   16CO142
  //   16CO144
endmodule

module T_Flip_Flops (
  input  _1,
  input  _2,
  input  _3,
  input  _4,
  input  _5,
  input  _6,
  input  _7,
  input  _8,
  input  _9,
  input  high,
  output q1,
  output q2,
  output q3,
  output q4,
  output q5,
  output q6,
  output q7,
  output q8,
  output q9
);

  T_Flip_Flop t_ff_1 (.clk(_1), .T(_1), .Q(q1), .en(high));  // open: Qn, preset, reset
  T_Flip_Flop t_ff_2 (.clk(_4), .T(_4), .Q(q4), .en(high));  // open: Qn, preset, reset
  T_Flip_Flop t_ff_3 (.clk(_7), .T(_7), .Q(q7), .en(high));  // open: Qn, preset, reset
  T_Flip_Flop t_ff_4 (.clk(_2), .T(_2), .Q(q2), .en(high));  // open: Qn, preset, reset
  T_Flip_Flop t_ff_5 (.clk(_5), .T(_5), .Q(q5), .en(high));  // open: Qn, preset, reset
  T_Flip_Flop t_ff_6 (.clk(_8), .T(_8), .Q(q8), .en(high));  // open: Qn, preset, reset
  T_Flip_Flop t_ff_7 (.clk(_3), .T(_3), .Q(q3), .en(high));  // open: Qn, preset, reset
  T_Flip_Flop t_ff_8 (.clk(_6), .T(_6), .Q(q6), .en(high));  // open: Qn, preset, reset
  T_Flip_Flop t_ff_9 (.clk(_9), .T(_9), .Q(q9), .en(high));  // open: Qn, preset, reset

  // Notes on the sheet:
  //   By:
  //   16CO142
  //   16CO144
endmodule

// Moves required finder
module Moves_Calucalator (
  input  i,
  input  i_2,
  input  i_3,
  input  i_4,
  input  i_5,
  input  i_6,
  input  i_7,
  input  i_8,
  input  i_9,
  input  hint,
  output a0,
  output a1,
  output a2,
  output a3
);

  wire full_adder_1_carry, full_adder_1_sum, full_adder_2_carry, full_adder_2_sum, full_adder_3_carry,
       full_adder_3_sum, full_adder_4_carry, full_adder_4_sum, full_adder_5_carry, full_adder_5_sum,
       half_adder_1_carry, half_adder_1_sum, half_adder_2_carry, half_adder_2_sum, half_adder_3_carry,
       half_adder_3_sum;

  Full_Adder full_adder_1 (.A(i), .B(i_2), .C(i_3), .sum(full_adder_1_sum), .carry(full_adder_1_carry));
  Full_Adder full_adder_2 (.A(i_4), .B(i_5), .C(i_6), .sum(full_adder_2_sum), .carry(full_adder_2_carry));
  Full_Adder full_adder_3 (.A(i_7), .B(i_8), .C(i_9), .sum(full_adder_3_sum), .carry(full_adder_3_carry));
  Half_Adder half_adder_1 (
    .a(full_adder_1_sum), .b(full_adder_2_sum), .sum(half_adder_1_sum), .carry(half_adder_1_carry));
  Full_Adder full_adder_4 (
    .A(half_adder_1_carry), .B(full_adder_1_carry), .C(full_adder_2_carry), .sum(full_adder_4_sum),
    .carry(full_adder_4_carry));
  Half_Adder half_adder_2 (
    .a(half_adder_1_sum), .b(full_adder_3_sum), .sum(half_adder_2_sum), .carry(half_adder_2_carry));
  Full_Adder full_adder_5 (
    .A(half_adder_2_carry), .B(full_adder_3_carry), .C(full_adder_4_sum), .sum(full_adder_5_sum),
    .carry(full_adder_5_carry));
  Half_Adder half_adder_3 (
    .a(full_adder_4_carry), .b(full_adder_5_carry), .sum(half_adder_3_sum), .carry(half_adder_3_carry));
  and and_1 (a0, half_adder_2_sum, hint);
  and and_2 (a1, full_adder_5_sum, hint);
  and and_3 (a2, half_adder_3_sum, hint);
  and and_4 (a3, half_adder_3_carry, hint);

  // Notes on the sheet:
  //   By:
  //   16CO142
  //   16CO144
endmodule

module Half_Adder (
  input  a,
  input  b,
  output sum,
  output carry
);

  xor xor_1 (sum, a, b);
  and and_1 (carry, a, b);

  // Notes on the sheet:
  //   By:
  //   16CO142
  //   16CO144
endmodule

module Full_Adder (
  input  A,
  input  B,
  input  C,
  output sum,
  output carry
);

  wire half_adder_1_carry, half_adder_1_sum, half_adder_2_carry;

  Half_Adder half_adder_1 (.a(B), .b(C), .sum(half_adder_1_sum), .carry(half_adder_1_carry));
  Half_Adder half_adder_2 (.a(A), .b(half_adder_1_sum), .sum(sum), .carry(half_adder_2_carry));
  or or_1 (carry, half_adder_2_carry, half_adder_1_carry);

  // Notes on the sheet:
  //   By:
  //   16CO142
  //   16CO144
endmodule

module Input_Controller (
  input  result,
  input  _1,
  input  _2,
  input  _3,
  input  _4,
  input  _5,
  input  _6,
  input  _7,
  input  _8,
  input  _9,
  output _1o,
  output _2o,
  output _3o,
  output _4o,
  output _5o,
  output _6o,
  output _7o,
  output _8o,
  output _9o
);

  and and_1 (_1o, _1, result);
  and and_2 (_2o, _2, result);
  and and_3 (_3o, _3, result);
  and and_4 (_4o, _4, result);
  and and_5 (_5o, _5, result);
  and and_6 (_6o, _6, result);
  and and_7 (_7o, _7, result);
  and and_8 (_8o, _8, result);
  and and_9 (_9o, _9, result);

  // Notes on the sheet:
  //   By:
  //   16CO142
  //   16CO144
endmodule

module Instruction_Module (
);


  // Notes on the sheet:
  //   GAME PLAY
  //   2.Your goal is to Switch OFF all the LED's with the use of INPUT pad
  //   8.If NO of MOVES made reaches 39 and still you didn't solve then You lost the Game
  //   1.When the Game Starts, Random pattern of lights is switched on pressing RESET(BLUE) button
  //   5.Press the corressponding button shown in LCD display when the HINT LED is on i.e,RED
  //   7.After the GAME IS SOLVED,press RESET button to paly again with different initial pattern
  //   NOTE: You can't return once you entered into the AUTOMATIC MODE until GAME IS OVER.If you do this you can't solve by these steps
  //   4.If you are unable to solve the GAME then press White button only ONCE in input section to go to the automatic mode
  //   3.On pressing any button in the INPUT PAD the  button itself and the very next  button to it in  all directions INVERSE their state(ON/OFF)
  //   6.Press the GREEN button 8 times to solve completely with taking care of 5TH point mentioned above after pressing GREEN button each time
endmodule

// Total no of moves Count
module Total_Moves_counter (
  input  high,
  input  clk,
  input  reset,
  output a2,
  output b2,
  output c2,
  output d2,
  output e2,
  output f2,
  output g2,
  output a1,
  output b1,
  output c1,
  output d1,
  output e,
  output f1,
  output gg1,
  output max
);

  wire and_2_out, counter_1_a0, counter_1_a1, counter_1_a2, counter_1_a3, counter_2_a0, counter_2_a1,
       counter_2_a2, counter_2_a3;

  LCD_Decoder lcd_decoder_1 (
    ._3(counter_1_a3), ._2(counter_1_a2), ._1(counter_1_a1), ._0(counter_1_a0), .a(a2), .b(b2), .c(c2),
    .d(d2), .e(e2), .f(f2), .g(g2));
  Counter counter_1 (
    .clk(clk), .high(and_2_out), .reset(reset), .a0(counter_1_a0), .a1(counter_1_a1), .a2(counter_1_a2),
    .a3(counter_1_a3));
  and and_1 (max, counter_1_a0, counter_1_a1, counter_2_a0, counter_2_a3);
  and and_2 (and_2_out, counter_2_a0, ~counter_2_a1, ~counter_2_a2, counter_2_a3);  // AND_Gate
  Counter counter_2 (
    .clk(clk), .high(high), .reset(reset), .a0(counter_2_a0), .a1(counter_2_a1), .a2(counter_2_a2),
    .a3(counter_2_a3));
  LCD_Decoder lcd_decoder_2 (
    ._3(counter_2_a3), ._2(counter_2_a2), ._1(counter_2_a1), ._0(counter_2_a0), .a(a1), .b(b1), .c(c1),
    .d(d1), .e(e), .f(f1), .g(gg1));

  // Notes on the sheet:
  //   By:
  //   16CO142
  //   16CO144
endmodule
